// Logisim project cpu.circ as structural Verilog: 4 circuits, main circuit ULA
module main (
  input  reset
);

  wire clk, cpu_1_out_8;
  wire [5:0] cpu_1_out_7;
  wire [7:0] cpu_1_out_5, cpu_1_out_6, ram_1_data, rom_1_data;

  Clock u_clk (.out(clk));
  CPU cpu_1 (
    .in_1(clk), .in_2(rom_1_data), .in_3(reset), .in_4(ram_1_data), .out_5(cpu_1_out_5), .out_6(cpu_1_out_6),
    .out_7(cpu_1_out_7), .out_8(cpu_1_out_8));
  ROM #(.addrWidth(6)) rom_1 (.addr(cpu_1_out_7), .data(rom_1_data));  // open: sel
  RAM #(.bus("separate")) ram_1 (
    .addr(cpu_1_out_6), .din(cpu_1_out_5), .data(ram_1_data), .str(cpu_1_out_8), .clk(clk), .ld(1'b1),
    .clr(reset));  // open: sel

  // Notes on the sheet:
  //   contents of rom_1 (hex, n*v repeats v):
  //   7f 63 71 74 78 75 63 72 5c 85
endmodule

module ULA (
  input  [7:0] A,
  input  [7:0] B,
  input  [1:0] S,
  output [7:0] out_4,
  output out_5
);

  wire [7:0] adder_1_out, and_1_out, multiplier_1_out, or_1_out;

  Adder adder_1 (.a(A), .b(B), .out(adder_1_out));  // open: cin, cout
  Multiplier multiplier_1 (.a(A), .b(B), .out(multiplier_1_out));  // open: cin, cout
  assign and_1_out = A & B;  // AND_Gate and_1, 8 bits wide
  assign or_1_out = A | B;  // OR_Gate or_1, 8 bits wide
  Comparator #(.mode("unsigned")) comparator_1 (.a(A), .b(B), .gt(out_5));  // open: eq, lt
  Multiplexer #(.select(2), .width(8)) multiplexer_1 (
    .in0(adder_1_out), .in1(multiplier_1_out), .in2(and_1_out), .in3(or_1_out), .out(out_4), .sel(S));  // open: en
endmodule

module REGS (
  input  [1:0] adda,
  input  [1:0] addb,
  input  [7:0] \input ,
  input  clk,
  input  reset,
  input  en,
  output [7:0] outa,
  output [7:0] outb
);

  wire en0, en1, en2, en3;
  wire [7:0] q0, q1, q2, q3;

  Register register_1 (.D(\input ), .en(en0), .Q(q0), .clk(clk), .clr(reset));
  Register register_2 (.D(\input ), .en(en2), .Q(q2), .clk(clk), .clr(reset));
  Multiplexer #(.select(2), .width(8)) multiplexer_1 (
    .in0(q0), .in1(q1), .in2(q2), .in3(q3), .out(outb), .sel(addb));  // open: en
  Register register_3 (.D(\input ), .en(en1), .Q(q1), .clk(clk), .clr(reset));
  Register register_4 (.D(\input ), .en(en3), .Q(q3), .clk(clk), .clr(reset));
  Multiplexer #(.select(2), .width(8)) multiplexer_2 (
    .in0(q0), .in1(q1), .in2(q2), .in3(q3), .out(outa), .sel(adda));  // open: en
  Demultiplexer #(.select(2)) demultiplexer_1 (
    .out0(en0), .out1(en1), .out2(en2), .out3(en3), .in(en), .sel(adda));  // open: en
endmodule

module CPU (
  input  in_1,
  input  [7:0] in_2,
  input  in_3,
  input  [7:0] in_4,
  output [7:0] out_5,
  output [7:0] out_6,
  output [5:0] out_7,
  output out_8
);

  wire and_7_out, cmp, isAdd, isAnd, isCmp, isLdr, isMov, isMul, isOr, isspecialcase, movecons, not_1_out,
       not_2_out, not_3_out, not_4_out, not_5_out, not_6_out, not_7_out, not_8_out, not_9_out, not_10_out,
       not_11_out, not_12_out, not_13_out, not_14_out, not_15_out, not_16_out, not_17_out, not_18_out,
       not_19_out, not_20_out, not_21_out, not_22_out, regen, ula_1_out_5;
  wire [1:0] multiplexer_4_out, op;
  wire [5:0] adder_1_out, nextline;
  wire [7:0] multiplexer_1_out, multiplexer_2_out, multiplexer_3_out, outula;

  Multiplexer #(.width(8)) multiplexer_1 (
    .in0(outula), .in1({{6{1'b0}}, in_2[1:0]}), .out(multiplexer_1_out), .sel(movecons));  // open: en
  Multiplexer #(.width(8)) multiplexer_2 (
    .in0(multiplexer_1_out), .in1(out_5), .out(multiplexer_2_out), .sel(isMov));  // open: en
  Multiplexer #(.width(8)) multiplexer_3 (
    .in0(multiplexer_2_out), .in1(in_4), .out(multiplexer_3_out), .sel(isLdr));  // open: en
  not not_1 (not_1_out, in_2[4]);
  not not_2 (not_2_out, in_2[7]);
  Register #(.width(6)) register_1 (.D(nextline), .en(in_1), .Q(out_7), .clk(in_1), .clr(in_3));
  Multiplexer #(.width(2)) multiplexer_4 (
    .in0(in_2[3:2]), .in1(2'b11), .out(multiplexer_4_out), .sel(isspecialcase));  // open: en
  Subtractor #(.width(2)) subtractor_1 (.a(in_2[5:4]), .b(2'b01), .out(op));  // open: bin, bout
  and and_1 (isMov, not_1_out, in_2[5], in_2[6], not_2_out);
  not not_3 (not_3_out, in_2[4]);
  not not_4 (not_4_out, in_2[5]);
  not not_5 (not_5_out, in_2[7]);
  not not_6 (not_6_out, in_2[2]);
  not not_7 (not_7_out, in_2[7]);
  REGS regs_1 (
    .adda(multiplexer_4_out), .addb(in_2[1:0]), .\input (multiplexer_3_out), .clk(in_1), .reset(in_3),
    .en(regen), .outa(out_6), .outb(out_5));
  Adder #(.width(6)) adder_1 (.a(out_7), .b(6'b000001), .out(adder_1_out));  // open: cin, cout
  not not_8 (not_8_out, in_2[5]);
  and and_2 (isAdd, in_2[4], not_8_out, not_9_out, not_10_out);
  not not_9 (not_9_out, in_2[6]);
  not not_10 (not_10_out, in_2[7]);
  not not_11 (not_11_out, in_2[4]);
  not not_12 (not_12_out, in_2[6]);
  and and_3 (isMul, not_11_out, in_2[5], not_12_out, not_13_out);
  not not_13 (not_13_out, in_2[7]);
  and and_4 (isAnd, in_2[4], in_2[5], not_14_out, not_15_out);
  not not_14 (not_14_out, in_2[6]);
  not not_15 (not_15_out, in_2[7]);
  and and_5 (isOr, not_3_out, not_4_out, in_2[6], not_5_out);
  and and_6 (isLdr, not_6_out, in_2[3], in_2[4], in_2[5], in_2[6], not_7_out);
  and and_7 (and_7_out, in_2[7], cmp);
  ULA ula_1 (.A(out_6), .B(out_5), .S(op), .out_4(outula), .out_5(ula_1_out_5));
  Multiplexer #(.width(6)) multiplexer_5 (
    .in0(adder_1_out), .in1(in_2[5:0]), .out(nextline), .sel(and_7_out));  // open: en
  not not_16 (not_16_out, in_2[2]);
  not not_17 (not_17_out, in_2[3]);
  not not_18 (not_18_out, in_2[7]);
  not not_19 (not_19_out, in_2[5]);
  not not_20 (not_20_out, in_2[7]);
  not not_21 (not_21_out, in_2[3]);
  not not_22 (not_22_out, in_2[7]);
  Register #(.width(1), .trigger("falling")) register_2 (.D(ula_1_out_5), .en(isCmp), .Q(cmp), .clk(in_1), .clr(in_3));
  and and_8 (movecons, not_16_out, not_17_out, in_2[4], in_2[5], in_2[6], not_18_out);
  or or_1 (isspecialcase, movecons, out_8, isLdr);
  and and_9 (isCmp, in_2[4], not_19_out, in_2[6], not_20_out);
  and and_10 (out_8, in_2[2], not_21_out, in_2[4], in_2[5], in_2[6], not_22_out);
  or or_2 (regen, isMov, isAdd, isMul, isLdr, isOr, movecons, isAnd);

  // Other names for the same wires on the sheet: address[5:0] = in_2[5:0]; opcode[7:0] = in_2; adda[1:0] = in_2[3:2];
  //   clk = in_1; addb[1:0] = in_2[1:0]; constant[1:0] = in_2[1:0]; isStr = out_8; memoryout[7:0] = in_4;
  //   isJmp = in_2[7]; memoryadd[7:0] = out_6; outA[7:0] = out_6; memorin[7:0] = out_5; outB[7:0] = out_5;
  //   PC[5:0] = out_7; reset = in_3
endmodule
